# Fritzing sketch Sensor de linea (saved by Fritzing 0.9.2b)
breadboards: 1

parts:
  Op1 = LMV324 [package=so014]
  R2 = TRIMPOT [package=trim_pot_pth]
  J1 = male pin header, 10 pins [form="♂ (male)"]
  Op2 = LMV324 [package=so014]
  pT1 = LTR-301 [package=ltr-301]
  R3 = Resistor [tolerance=±5% resistance=220 package=THT]
  pT2 = LTR-301 [package=ltr-301]
  R4 = Resistor [tolerance=±5% resistance=220 package=THT]
  pT3 = LTR-301 [package=ltr-301]
  R5 = Resistor [tolerance=±5% resistance=220 package=THT]
  pT4 = LTR-301 [package=ltr-301]
  R6 = Resistor [tolerance=±5% resistance=220 package=THT]
  pT5 = LTR-301 [package=ltr-301]
  R7 = Resistor [tolerance=±5% resistance=220 package=THT]
  pT6 = LTR-301 [package=ltr-301]
  R8 = Resistor [tolerance=±5% resistance=220 package=THT]
  pT7 = LTR-301 [package=ltr-301]
  R9 = Resistor [tolerance=±5% resistance=220 package=THT]
  pT8 = LTR-301 [package=ltr-301]
  R10 = Resistor [tolerance=±5% resistance=220 package=THT]
  IC1 = MICROCONTROLLER [package=dil28-3]
  S1 = SWITCH-MOMENTARY-2 [package=tactile-pth]
  R11 = Resistor [tolerance=±5% resistance=10k package=THT]
  XTAL1 = Crystal [frequency="16 Mhz" package=THT]
  C1 = Ceramic Capacitor [capacitance=22pF package="0603 [SMD, multilayer]"]
  C2 = Ceramic Capacitor [capacitance=22pF package="0603 [SMD, multilayer]"]
  HC-SR04_1 = female pin header, 4 pins [form="♀ (female)"]
  IC2 = Voltage Regulator [package=to-220-alt]
  C3 = Electrolytic Capacitor [capacitance=1µF voltage=16V package="100 mil [THT, electrolytic]"]
  C4 = Electrolytic Capacitor [capacitance=10µF voltage=16V package="100 mil [THT, electrolytic]"]
  D1 = Diode [package=diode-1n4001]
  HC-SR04_2 = female pin header, 4 pins [form="♀ (female)"]
  mDriver = ULN2003A [package="DIP16 [THT]"]
  Motor1 = female pin header, 2 pins [form="♀ (female)"]
  Motor2 = female pin header, 2 pins [form="♀ (female)"]

nets:
  p1: Op1.G$1_OUT, J1.pin1, IC1.PD2(INT0)
  vPot: Op1.G$1_-IN, Op1.G$2_-IN, Op1.G$3_-IN, Op1.G$4_-IN, R2.WIPER, Op2.G$1_-IN, Op2.G$2_-IN, Op2.G$3_-IN, Op2.G$4_-IN
  vpT1: Op1.G$1_+IN, pT1.C, R3.Pin_1
  5V: Op1.G$1_+V, R2.CCW, J1.pin9, R3.Pin_0, R4.Pin_0, R5.Pin_0, R6.Pin_0, R7.Pin_0, R8.Pin_0, R9.Pin_0, R10.Pin_0, IC1.VCC, IC1.AVCC, S1.2, R11.Pin_0, HC-SR04_1.pin1, IC2.OUT, C3.+, HC-SR04_2.pin1
  vpT2: Op1.G$2_+IN, pT2.C, R4.Pin_1
  p2: Op1.G$2_OUT, J1.pin2, IC1.PD4(XCK_T0)
  p3: Op1.G$3_OUT, J1.pin3, IC1.PD7(AIN1)
  vpT3: Op1.G$3_+IN, pT3.C, R5.Pin_1
  GND: Op1.G$1_-V, R2.CW, J1.pin10, pT1.E, pT2.E, pT3.E, pT4.E, pT5.E, pT6.E, pT7.E, pT8.E, IC1.GND, IC1.AGND, S1.1, C1.1, C2.1, HC-SR04_1.pin4, IC2.GND, C3.-, C4.-, D1.A, HC-SR04_2.pin4, mDriver.0V
  vpT4: Op1.G$4_+IN, pT4.C, R6.Pin_1
  p4: Op1.G$4_OUT, J1.pin4, IC1.PB0(ICP)
  p5: J1.pin5, Op2.G$1_OUT, IC1.PB4(MISO)
  p6: J1.pin6, Op2.G$2_OUT, IC1.PB5(SCK)
  p7: J1.pin7, Op2.G$3_OUT, IC1.PC0(ADC0)
  p8: J1.pin8, Op2.G$4_OUT, IC1.PC1(ADC1)
  vpT5: Op2.G$1_+IN, pT5.C, R7.Pin_1
  vpT6: Op2.G$2_+IN, pT6.C, R8.Pin_1
  vpT7: Op2.G$3_+IN, pT7.C, R9.Pin_1
  vpT8: Op2.G$4_+IN, pT8.C, R10.Pin_1
  N1: IC1.PC6(_RESET), R11.Pin_1
  N2: IC1.PB6(XTAL1_TOSC1), XTAL1.pin_1, C1.0
  N3: IC1.PB7(XTAL2_TOSC2), XTAL1.pin_0, C2.0
  MPin1: IC1.PD5(T1), mDriver.In_1
  MPin2: IC1.PD6(AIN0), mDriver.In_2
  Trigger1: HC-SR04_1.pin2
  Echo1: HC-SR04_1.pin3
  12V: IC2.IN, C4.+, D1.C, mDriver.COM_-_Common, Motor1.pin2, Motor2.pin2
  Trigger2: HC-SR04_2.pin2
  Echo2: HC-SR04_2.pin3
  N4: mDriver.Out_2, Motor2.pin1
  N5: mDriver.Out_1, Motor1.pin1
